# Fritzing sketch Connections-ESP32-LoRaSX1278 (saved by Fritzing 0.9.3b)
perfboards: 2

parts:
  M2 = DOIT Esp32 DevKit v1 (30 pins long, 11 pins width) [part_number=ESP32S-PIN30]
  M3 = Osoyoo SX1278-ra-02
  M4 = DOIT Esp32 DevKit v1 (30 pins long, 11 pins width) [part_number=ESP32S-PIN30]  # not connected
  M5 = Osoyoo SX1278-ra-02  # not connected
  J1 = female pin header, 15 pins [form="♀ (female)"]
  J2 = female pin header, 15 pins [form="♀ (female)"]  # not connected
  J3 = female pin header, 8 pins [form="♀ (female)"]
  J4 = female pin header, 8 pins [form="♀ (female)"]

nets:
  3V3: M2.3V3, M2.D15, M3.3.3V, M3.RST
  GND: M2.GND, M3.GND
  N1: M2.D2, M3.DIO0
  N2: M2.D5, M3.NSS
  N3: M2.D18, M3.MOSI
  N4: M2.D22, M3.MISO
  N5: M2.D23, M3.SCK
  N6: J1.pin1, J3.pin5
  N7: J1.pin2, J3.pin4
  N8: J1.pin7, J3.pin3
  N9: J1.pin8, J3.pin2
  N10: J1.pin12, J4.pin5
  N11: J1.pin13, J4.pin4
  N12: J1.pin14, J4.pin2
  N13: J1.pin15, J4.pin3

custom parts:
  DOIT Esp32 DevKit v1 (30 pins long, 11 pins width): The DOIT Esp32 DevKit v1 is one of the development board created by DOIT to evaluate the ESP-WROOM-32 module. It is based on the ESP32 microcontroller that boasts Wifi, Bluetooth, Ethernet and Low Power support all in a single chip. (vanepp) made breadboard work, adjusted pin numbering and labels and reduced size of schematic and cleaned up pcb. This chip is 30pins long (2 x15) and 11 pins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
  Osoyoo SX1278-ra-02: Osoyoo Long Distance wireless transceiver Uart LoRa Module.
