# Fritzing sketch _old_Prototype-ESP32-FLEX-MPU-MAX-Conections (saved by Fritzing 0.9.3b)

parts:
  M1 = gy9250
  M2 = MakerFocus MAX30102
  R2 = Resistor [tolerance=±5% resistance=10k package="2512 [SMD]"]
  J2 = female pin header, 1 pin [form="♀ (female)"]
  J3 = female pin header, 1 pin [form="♀ (female)"]
  J5 = female pin header, 1 pin [form="♀ (female)"]
  J4 = female pin header, 1 pin [form="♀ (female)"]
  J6 = female pin header, 1 pin [form="♀ (female)"]
  R1 = Basic Flex Resistor
  A7 = Esp32-c3 super mini

nets:
  N1: M1.pin1, M2.VIN, J3.pin1, J6.pin1, R1.Pin_2, A7.Pin_14
  N2: M1.pin2, R2.Pin_0, J2.pin1
  N3: M1.pin3, A7.Pin_9
  N4: M1.pin4, A7.Pin_10
  N5: M2.GND, J4.pin1, A7.Pin_15
  N6: M2.SCL, A7.Pin_13
  N7: M2.SDA, A7.Pin_4
  N8: R2.Pin_1, J5.pin1, R1.pin_1, A7.Pin_12

custom parts:
  gy9250: MPU-9250 module (three-axis gyroscope + three-axis acceleration + three-axis magnetic field). The generic model from ebay et. al. rather than the Sparkfun version.
  MakerFocus MAX30102: Oximeter module using the MAX30102 chip. As usual, if you want the mounting holes in pcb, you need to drag a hole over the pad in silkscreen to actually drill the hole (by default they are not drilled)
  Esp32-c3 super mini: ESP32-C3 Development Board ESP32 SuperMini Development Board ESP32 Development Board WiFi Bluetooth.
