# Fritzing sketch 2_Scheme-ESP32-FLEX-MPU-MAX (saved by Fritzing 0.9.3b)
perfboards: 2

parts:
  A9 = Esp32-c3 super mini  # not connected
  M3 = gy9250  # not connected
  Mod2 = AD8232 HeartRate Monitor [part_number=SEN-12650]  # not connected
  A10 = Esp32-c3 super mini  # not connected
  J3 = female pin header, 6 pins [form="♀ (female)"]
  J4 = male pin header, 6 pins [form="♂ (male)"]
  J5 = female pin header, 10 pins [form="♀ (female)"]
  J6 = male pin header, 4 pins [form="♂ (male)"]

nets:
  N1: J3.pin1, J4.pin6
  N2: J3.pin2, J4.pin5
  N3: J3.pin3, J4.pin4
  N4: J3.pin4, J4.pin3
  N5: J3.pin5, J4.pin2
  N6: J3.pin6, J4.pin1
  N7: J5.pin1, J6.pin4
  N8: J5.pin2, J6.pin3
  N9: J5.pin3, J6.pin2
  N10: J5.pin4, J6.pin1

custom parts:
  Esp32-c3 super mini: ESP32-C3 Development Board ESP32 SuperMini Development Board ESP32 Development Board WiFi Bluetooth.
  gy9250: MPU-9250 module (three-axis gyroscope + three-axis acceleration + three-axis magnetic field). The generic model from ebay et. al. rather than the Sparkfun version.
  AD8232 HeartRate Monitor: Sparkfun single lead heart rate monitor - Ad8232.
