# Fritzing sketch Liligo7070g_LoRa_SX1278_Gateway (saved by Fritzing 0.9.3b)
perfboards: 1

parts:
  M3 = Osoyoo SX1278-ra-02
  M4 = LILYGO TTGO-T SIM7000G
  J1 = female pin header, 16 pins [form="♀ (female)"]  # not connected
  J2 = female pin header, 16 pins [form="♀ (female)"]
  J3 = female pin header, 8 pins [form="♀ (female)"]
  J4 = female pin header, 8 pins [form="♀ (female)"]

nets:
  N1: M3.GND, M4.pin_2, M4.pin_29
  N2: M3.3.3V, M3.RST, M4.pin_1, M4.pin_27, M4.pin_30
  N3: M3.DIO0, M4.pin_28
  N4: M3.SCK, M4.pin_24
  N5: M3.MISO, M4.pin_25
  N6: M3.MOSI, M4.pin_26
  N7: M3.NSS, M4.pin_23
  N8: J2.pin3, J4.pin3
  N9: J2.pin4, J4.pin2
  N10: J2.pin5, J4.pin5
  N11: J2.pin6, J4.pin4
  N12: J2.pin7, J3.pin3
  N13: J2.pin8, J3.pin4
  N14: J2.pin9, J3.pin5
  N15: J2.pin10, J3.pin2

custom parts:
  Osoyoo SX1278-ra-02: Osoyoo Long Distance wireless transceiver Uart LoRa Module.
  LILYGO TTGO-T SIM7000G: LILYGO® TTGO T-SIM7000G Module ESP32-WROVER-B Chip WiFi Bluetooth 18560 Battery Holder Solar Charge Development Board.
