# Fritzing sketch Liligo7070g_LoRa_SX1278_Gateway (saved by Fritzing 0.9.3b)

parts:
  M1 = Osoyoo SX1278-ra-02
  U1 = ESP32-38PinWide [part_number=ESP32-38PinWide]
  M2 = DOIT Esp32 DevKit v1 (30 pins long, 11 pins width) [part_number=ESP32S-PIN30]
  M3 = Osoyoo SX1278-ra-02

nets:
  GND: M1.GND, U1.GND
  N1: M1.3.3V, U1.3.3
  N2: M1.RST, U1.GPIO23
  N3: M1.DIO0, U1.GPIO4
  N4: M1.SCK, U1.GPIO33
  N5: M1.MISO, U1.GPIO35
  N6: M1.MOSI, U1.GPIO32
  N7: M1.NSS, U1.GPIO15
  3V3: M2.3V3, M2.D15, M3.3.3V, M3.RST
  GND_2: M2.GND, M3.GND
  N8: M2.D2, M3.DIO0
  N9: M2.D5, M3.NSS
  N10: M2.D18, M3.MOSI
  N11: M2.D22, M3.MISO
  N12: M2.D23, M3.SCK

custom parts:
  Osoyoo SX1278-ra-02: Osoyoo Long Distance wireless transceiver Uart LoRa Module.
  ESP32-38PinWide: Generic 38-Pin ESP32 with wide format (only access to one side of pins on a breadboard) based on Stephen Lilley's HiLetgo ESP-WROOM-32 ESP32 ESP-32S Development Board.
  DOIT Esp32 DevKit v1 (30 pins long, 11 pins width): The DOIT Esp32 DevKit v1 is one of the development board created by DOIT to evaluate the ESP-WROOM-32 module. It is based on the ESP32 microcontroller that boasts Wifi, Bluetooth, Ethernet and Low Power support all in a single chip. (vanepp) made breadboard work, adjusted pin numbering and labels and reduced size of schematic and cleaned up pcb. This chip is 30pins long (2 x15) and 11 pins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
