# Fritzing sketch Prototype-ESP32-FLEX-MPU-MAX (saved by Fritzing 0.9.3b)
# 18650 Li-ion Battery: CC-BY Dr Kristofer Chan, King's College London/Remote-research.org
perfboards: 2

parts:
  M1 = gy9250
  M2 = MakerFocus MAX30102
  R2 = Resistor [tolerance=±5% resistance=10k package="2512 [SMD]"]
  J2 = female pin header, 1 pin [form="♀ (female)"]
  J3 = female pin header, 1 pin [form="♀ (female)"]
  J5 = female pin header, 1 pin [form="♀ (female)"]
  J4 = female pin header, 1 pin [form="♀ (female)"]
  J6 = female pin header, 1 pin [form="♀ (female)"]
  R1 = Basic Flex Resistor
  A7 = Esp32-c3 super mini
  A9 = Esp32-c3 super mini  # not connected
  BAT2 = 18650 Li-ion Battery [package=battery-18650]  # not connected
  MOD2 = MT3608 Boost No usb  # not connected
  M5 = gy9250  # not connected
  M6 = MakerFocus MAX30102  # not connected
  R5 = Basic Flex Resistor  # not connected
  J8 = female pin header, 4 pins [form="♀ (female)"]  # not connected
  J9 = female pin header, 4 pins [form="♀ (female)"]
  J10 = female pin header, 8 pins [form="♀ (female)"]
  J11 = female pin header, 8 pins [form="♀ (female)"]
  J12 = female pin header, 10 pins [form="♀ (female)"]
  J13 = female pin header, 1 pin [form="♀ (female)"]
  J14 = female pin header, 1 pin [form="♀ (female)"]
  J15 = female pin header, 1 pin [form="♀ (female)"]  # not connected
  J16 = female pin header, 1 pin [form="♀ (female)"]  # not connected
  R6 = Basic Flex Resistor
  R7 = Resistor [tolerance=±5% resistance=10k package="2512 [SMD]"]

nets:
  N1: M1.pin1, M2.VIN, J3.pin1, J6.pin1, R1.Pin_2, A7.Pin_14
  N2: M1.pin2, R2.Pin_0, J2.pin1
  N3: M1.pin3, A7.Pin_9
  N4: M1.pin4, A7.Pin_10
  N5: M2.GND, J4.pin1, A7.Pin_15
  N6: M2.SCL, A7.Pin_13
  N7: M2.SDA, A7.Pin_4
  N8: R2.Pin_1, J5.pin1, R1.pin_1, A7.Pin_12
  N9: J9.pin2, J11.pin4
  N10: J9.pin3, J10.pin4
  N11: J9.pin4, J10.pin2, J14.pin1
  N12: J10.pin1, J13.pin1
  N13: J10.pin3, R6.pin_1
  N14: J10.pin7, J12.pin4
  N15: J10.pin8, J12.pin3
  N16: R6.Pin_2, R7.Pin_0

custom parts:
  gy9250: MPU-9250 module (three-axis gyroscope + three-axis acceleration + three-axis magnetic field). The generic model from ebay et. al. rather than the Sparkfun version.
  MakerFocus MAX30102: Oximeter module using the MAX30102 chip. As usual, if you want the mounting holes in pcb, you need to drag a hole over the pad in silkscreen to actually drill the hole (by default they are not drilled)
  Esp32-c3 super mini: ESP32-C3 Development Board ESP32 SuperMini Development Board ESP32 Development Board WiFi Bluetooth.
  18650 Li-ion Battery: 18650 li-ion Battery Standard 18650 battery with interactive connectors Creative Common Attribution 4.0 International (CC-BY 4.0) license. Any use of this part requires attribution of Dr Kristofer Chan, Department of Geography, King's College London. Contact kristofer.chan [at] kcl.ac.uk OR kris [at] remote-research.org for further information.
  MT3608 Boost No usb: Chip- MT3608 / B6289 DC to DC step up, power booster module. With adjustable output voltage. Current- 2A . || Input voltage- 2V-24V || Output voltage- 5V-28V Input interface- Inversed polarity- NO. || Led indicator- No.
