# Fritzing sketch TEST-ESP32-FLEX-MPU-MAX (saved by Fritzing 0.9.3b)
breadboards: 1

parts:
  M2 = MakerFocus MAX30102
  R1 = Basic Flex Resistor
  U1 = ESP32-38PinWide [part_number=ESP32-38PinWide]
  M1 = gy9250
  R2 = Resistor [tolerance=±5% resistance=10k package="1206 [SMD]"]

nets:
  GND: M2.GND, U1.GND, M1.pin2, R2.Pin_1
  N1: M2.SCL, U1.GPIO27
  N2: M2.SDA, U1.GPIO26
  N3: M2.VIN, R1.Pin_2, U1.EN, M1.pin1
  N4: R1.pin_1, U1.GPIO25, R2.Pin_0
  N5: U1.GPIO32, M1.pin3
  N6: U1.GPIO33, M1.pin4

custom parts:
  MakerFocus MAX30102: Oximeter module using the MAX30102 chip. As usual, if you want the mounting holes in pcb, you need to drag a hole over the pad in silkscreen to actually drill the hole (by default they are not drilled)
  ESP32-38PinWide: Generic 38-Pin ESP32 with wide format (only access to one side of pins on a breadboard) based on Stephen Lilley's HiLetgo ESP-WROOM-32 ESP32 ESP-32S Development Board.
  gy9250: MPU-9250 module (three-axis gyroscope + three-axis acceleration + three-axis magnetic field). The generic model from ebay et. al. rather than the Sparkfun version.
